# Fritzing sketch OpiShutdown (saved by Fritzing 0.9.2b)
breadboards: 1

parts:
  S1 = Pushbutton [package="[THT]"]
  R1 = Resistor [tolerance=±5% resistance=10k package="0402 [SMD]"]
  R2 = Resistor [tolerance=±5% resistance=1k package="0402 [SMD]"]

nets:
  N1: S1.Pin_1, S1.Pin_2, R1.Pin_1, R2.Pin_0
  N2: S1.Pin_3, S1.Pin_4
